// Logisim project and16_gate.circ as structural Verilog: 1 circuit, main circuit main
module main (
  input  a_16,
  input  in_2,
  input  in_3,
  input  in_4,
  input  in_5,
  input  in_6,
  input  in_7,
  input  in_8,
  input  in_9,
  input  in_10,
  input  in_11,
  input  in_12,
  input  in_13,
  input  in_14,
  input  in_15,
  input  in_16,
  input  b_16,
  input  in_18,
  input  in_19,
  input  in_20,
  input  in_21,
  input  in_22,
  input  in_23,
  input  in_24,
  input  in_25,
  input  in_26,
  input  in_27,
  input  in_28,
  input  in_29,
  input  in_30,
  input  in_31,
  input  in_32,
  output out_16,
  output out_34,
  output out_35,
  output out_36,
  output out_37,
  output out_38,
  output out_39,
  output out_40,
  output out_41,
  output out_42,
  output out_43,
  output out_44,
  output out_45,
  output out_46,
  output out_47,
  output out_48
);

  and AND (out_16, a_16, b_16);
  and AND_2 (out_34, in_2, in_18);
  and AND_3 (out_35, in_3, in_19);
  and AND_4 (out_36, in_4, in_20);
  and AND_5 (out_37, in_5, in_21);
  and AND_6 (out_38, in_6, in_22);
  and AND_7 (out_39, in_7, in_23);
  and AND_8 (out_40, in_8, in_24);
  and AND_9 (out_41, in_9, in_25);
  and AND_10 (out_42, in_10, in_26);
  and AND_11 (out_43, in_11, in_27);
  and AND_12 (out_44, in_12, in_28);
  and AND_13 (out_45, in_13, in_29);
  and AND_14 (out_46, in_14, in_30);
  and AND_15 (out_47, in_15, in_31);
  and AND_16 (out_48, in_16, in_32);
endmodule
