// Logisim project and_gate.circ as structural Verilog: 1 circuit, main circuit main
module main (
  input  a,
  input  b,
  output out_3
);

  wire NAND_2_out, NAND_out;

  nand NAND (NAND_out, a, b);
  nand NAND_2 (NAND_2_out, a, b);
  nand NAND_3 (out_3, NAND_out, NAND_2_out);
endmodule
