// Logisim project dmux4way_gate.circ as structural Verilog: 1 circuit, main circuit main
module main (
  input  in,
  input  sel_1,
  input  sel_0,
  output a,
  output b,
  output c,
  output d
);

  wire demultiplexer_1_out0, demultiplexer_1_out1;

  Demultiplexer #(.enable("false")) demultiplexer_1 (
    .out0(demultiplexer_1_out0), .out1(demultiplexer_1_out1), .in(in), .sel(sel_1));
  Demultiplexer #(.enable("false")) demultiplexer_2 (.out0(a), .out1(b), .in(demultiplexer_1_out0), .sel(sel_0));
  Demultiplexer #(.enable("false")) demultiplexer_3 (.out0(c), .out1(d), .in(demultiplexer_1_out1), .sel(sel_0));
endmodule
