// Logisim project dmux8way_gate.circ as structural Verilog: 1 circuit, main circuit main
module main (
  input  in,
  input  sel_2,
  input  sel_1,
  input  sel_0,
  output a,
  output b,
  output c,
  output d,
  output e,
  output f,
  output g,
  output h
);

  wire demultiplexer_1_out0, demultiplexer_1_out1, demultiplexer_2_out0, demultiplexer_2_out1,
       demultiplexer_3_out0, demultiplexer_3_out1;

  Demultiplexer #(.enable("false")) demultiplexer_1 (
    .out0(demultiplexer_1_out0), .out1(demultiplexer_1_out1), .in(demultiplexer_2_out0), .sel(sel_1));
  Demultiplexer #(.enable("false")) demultiplexer_2 (
    .out0(demultiplexer_2_out0), .out1(demultiplexer_2_out1), .in(in), .sel(sel_2));
  Demultiplexer #(.enable("false")) demultiplexer_3 (
    .out0(demultiplexer_3_out0), .out1(demultiplexer_3_out1), .in(demultiplexer_2_out1), .sel(sel_1));
  Demultiplexer #(.enable("false")) demultiplexer_4 (.out0(a), .out1(b), .in(demultiplexer_1_out0), .sel(sel_0));
  Demultiplexer #(.enable("false")) demultiplexer_5 (.out0(c), .out1(d), .in(demultiplexer_1_out1), .sel(sel_0));
  Demultiplexer #(.enable("false")) demultiplexer_6 (.out0(e), .out1(f), .in(demultiplexer_3_out0), .sel(sel_0));
  Demultiplexer #(.enable("false")) demultiplexer_7 (.out0(g), .out1(h), .in(demultiplexer_3_out1), .sel(sel_0));
endmodule
