// Logisim project dmux_gate.circ as structural Verilog: 1 circuit, main circuit main
module main (
  input  in,
  input  sel,
  output a,
  output b
);

  wire not_1_out;

  not not_1 (not_1_out, sel);
  and AND (a, in, not_1_out);
  and AND_2 (b, in, sel);
endmodule
