// Logisim project mux4way16_gate.circ as structural Verilog: 1 circuit, main circuit main
module main (
  input  a_16,
  input  in_2,
  input  in_3,
  input  in_4,
  input  in_5,
  input  in_6,
  input  in_7,
  input  in_8,
  input  in_9,
  input  in_10,
  input  in_11,
  input  in_12,
  input  in_13,
  input  in_14,
  input  in_15,
  input  in_16,
  input  b_16,
  input  in_18,
  input  in_19,
  input  in_20,
  input  in_21,
  input  in_22,
  input  in_23,
  input  in_24,
  input  in_25,
  input  in_26,
  input  in_27,
  input  in_28,
  input  in_29,
  input  in_30,
  input  in_31,
  input  in_32,
  input  c_16,
  input  in_34,
  input  in_35,
  input  in_36,
  input  in_37,
  input  in_38,
  input  in_39,
  input  in_40,
  input  in_41,
  input  in_42,
  input  in_43,
  input  in_44,
  input  in_45,
  input  in_46,
  input  in_47,
  input  in_48,
  input  d_16,
  input  in_50,
  input  in_51,
  input  in_52,
  input  in_53,
  input  in_54,
  input  in_55,
  input  in_56,
  input  in_57,
  input  in_58,
  input  in_59,
  input  in_60,
  input  in_61,
  input  in_62,
  input  in_63,
  input  in_64,
  input  sel_1,
  input  sel_0,
  output out_16,
  output out_68,
  output out_69,
  output out_70,
  output out_71,
  output out_72,
  output out_73,
  output out_74,
  output out_75,
  output out_76,
  output out_77,
  output out_78,
  output out_79,
  output out_80,
  output out_81,
  output out_82
);

  wire multiplexer_1_out, multiplexer_3_out, multiplexer_4_out, multiplexer_6_out, multiplexer_7_out,
       multiplexer_9_out, multiplexer_10_out, multiplexer_12_out, multiplexer_13_out, multiplexer_15_out,
       multiplexer_16_out, multiplexer_18_out, multiplexer_19_out, multiplexer_21_out, multiplexer_22_out,
       multiplexer_24_out, multiplexer_25_out, multiplexer_27_out, multiplexer_28_out, multiplexer_30_out,
       multiplexer_31_out, multiplexer_33_out, multiplexer_34_out, multiplexer_36_out, multiplexer_37_out,
       multiplexer_39_out, multiplexer_40_out, multiplexer_42_out, multiplexer_43_out, multiplexer_45_out,
       multiplexer_46_out, multiplexer_48_out;

  Multiplexer #(.enable("false")) multiplexer_1 (.in0(a_16), .in1(b_16), .out(multiplexer_1_out), .sel(sel_0));
  Multiplexer #(.enable("false")) multiplexer_2 (
    .in0(multiplexer_1_out), .in1(multiplexer_3_out), .out(out_16), .sel(sel_1));
  Multiplexer #(.enable("false")) multiplexer_3 (.in0(c_16), .in1(d_16), .out(multiplexer_3_out), .sel(sel_0));
  Multiplexer #(.enable("false")) multiplexer_4 (.in0(in_2), .in1(in_18), .out(multiplexer_4_out), .sel(sel_0));
  Multiplexer #(.enable("false")) multiplexer_5 (
    .in0(multiplexer_4_out), .in1(multiplexer_6_out), .out(out_68), .sel(sel_1));
  Multiplexer #(.enable("false")) multiplexer_6 (.in0(in_34), .in1(in_50), .out(multiplexer_6_out), .sel(sel_0));
  Multiplexer #(.enable("false")) multiplexer_7 (.in0(in_3), .in1(in_19), .out(multiplexer_7_out), .sel(sel_0));
  Multiplexer #(.enable("false")) multiplexer_8 (
    .in0(multiplexer_7_out), .in1(multiplexer_9_out), .out(out_69), .sel(sel_1));
  Multiplexer #(.enable("false")) multiplexer_9 (.in0(in_35), .in1(in_51), .out(multiplexer_9_out), .sel(sel_0));
  Multiplexer #(.enable("false")) multiplexer_10 (.in0(in_4), .in1(in_20), .out(multiplexer_10_out), .sel(sel_0));
  Multiplexer #(.enable("false")) multiplexer_11 (
    .in0(multiplexer_10_out), .in1(multiplexer_12_out), .out(out_70), .sel(sel_1));
  Multiplexer #(.enable("false")) multiplexer_12 (.in0(in_36), .in1(in_52), .out(multiplexer_12_out), .sel(sel_0));
  Multiplexer #(.enable("false")) multiplexer_13 (.in0(in_5), .in1(in_21), .out(multiplexer_13_out), .sel(sel_0));
  Multiplexer #(.enable("false")) multiplexer_14 (
    .in0(multiplexer_13_out), .in1(multiplexer_15_out), .out(out_71), .sel(sel_1));
  Multiplexer #(.enable("false")) multiplexer_15 (.in0(in_37), .in1(in_53), .out(multiplexer_15_out), .sel(sel_0));
  Multiplexer #(.enable("false")) multiplexer_16 (.in0(in_6), .in1(in_22), .out(multiplexer_16_out), .sel(sel_0));
  Multiplexer #(.enable("false")) multiplexer_17 (
    .in0(multiplexer_16_out), .in1(multiplexer_18_out), .out(out_72), .sel(sel_1));
  Multiplexer #(.enable("false")) multiplexer_18 (.in0(in_38), .in1(in_54), .out(multiplexer_18_out), .sel(sel_0));
  Multiplexer #(.enable("false")) multiplexer_19 (.in0(in_7), .in1(in_23), .out(multiplexer_19_out), .sel(sel_0));
  Multiplexer #(.enable("false")) multiplexer_20 (
    .in0(multiplexer_19_out), .in1(multiplexer_21_out), .out(out_73), .sel(sel_1));
  Multiplexer #(.enable("false")) multiplexer_21 (.in0(in_39), .in1(in_55), .out(multiplexer_21_out), .sel(sel_0));
  Multiplexer #(.enable("false")) multiplexer_22 (.in0(in_8), .in1(in_24), .out(multiplexer_22_out), .sel(sel_0));
  Multiplexer #(.enable("false")) multiplexer_23 (
    .in0(multiplexer_22_out), .in1(multiplexer_24_out), .out(out_74), .sel(sel_1));
  Multiplexer #(.enable("false")) multiplexer_24 (.in0(in_40), .in1(in_56), .out(multiplexer_24_out), .sel(sel_0));
  Multiplexer #(.enable("false")) multiplexer_25 (.in0(in_9), .in1(in_25), .out(multiplexer_25_out), .sel(sel_0));
  Multiplexer #(.enable("false")) multiplexer_26 (
    .in0(multiplexer_25_out), .in1(multiplexer_27_out), .out(out_75), .sel(sel_1));
  Multiplexer #(.enable("false")) multiplexer_27 (.in0(in_41), .in1(in_57), .out(multiplexer_27_out), .sel(sel_0));
  Multiplexer #(.enable("false")) multiplexer_28 (.in0(in_10), .in1(in_26), .out(multiplexer_28_out), .sel(sel_0));
  Multiplexer #(.enable("false")) multiplexer_29 (
    .in0(multiplexer_28_out), .in1(multiplexer_30_out), .out(out_76), .sel(sel_1));
  Multiplexer #(.enable("false")) multiplexer_30 (.in0(in_42), .in1(in_58), .out(multiplexer_30_out), .sel(sel_0));
  Multiplexer #(.enable("false")) multiplexer_31 (.in0(in_11), .in1(in_27), .out(multiplexer_31_out), .sel(sel_0));
  Multiplexer #(.enable("false")) multiplexer_32 (
    .in0(multiplexer_31_out), .in1(multiplexer_33_out), .out(out_77), .sel(sel_1));
  Multiplexer #(.enable("false")) multiplexer_33 (.in0(in_43), .in1(in_59), .out(multiplexer_33_out), .sel(sel_0));
  Multiplexer #(.enable("false")) multiplexer_34 (.in0(in_12), .in1(in_28), .out(multiplexer_34_out), .sel(sel_0));
  Multiplexer #(.enable("false")) multiplexer_35 (
    .in0(multiplexer_34_out), .in1(multiplexer_36_out), .out(out_78), .sel(sel_1));
  Multiplexer #(.enable("false")) multiplexer_36 (.in0(in_44), .in1(in_60), .out(multiplexer_36_out), .sel(sel_0));
  Multiplexer #(.enable("false")) multiplexer_37 (.in0(in_13), .in1(in_29), .out(multiplexer_37_out), .sel(sel_0));
  Multiplexer #(.enable("false")) multiplexer_38 (
    .in0(multiplexer_37_out), .in1(multiplexer_39_out), .out(out_79), .sel(sel_1));
  Multiplexer #(.enable("false")) multiplexer_39 (.in0(in_45), .in1(in_61), .out(multiplexer_39_out), .sel(sel_0));
  Multiplexer #(.enable("false")) multiplexer_40 (.in0(in_14), .in1(in_30), .out(multiplexer_40_out), .sel(sel_0));
  Multiplexer #(.enable("false")) multiplexer_41 (
    .in0(multiplexer_40_out), .in1(multiplexer_42_out), .out(out_80), .sel(sel_1));
  Multiplexer #(.enable("false")) multiplexer_42 (.in0(in_46), .in1(in_62), .out(multiplexer_42_out), .sel(sel_0));
  Multiplexer #(.enable("false")) multiplexer_43 (.in0(in_15), .in1(in_31), .out(multiplexer_43_out), .sel(sel_0));
  Multiplexer #(.enable("false")) multiplexer_44 (
    .in0(multiplexer_43_out), .in1(multiplexer_45_out), .out(out_81), .sel(sel_1));
  Multiplexer #(.enable("false")) multiplexer_45 (.in0(in_47), .in1(in_63), .out(multiplexer_45_out), .sel(sel_0));
  Multiplexer #(.enable("false")) multiplexer_46 (.in0(in_16), .in1(in_32), .out(multiplexer_46_out), .sel(sel_0));
  Multiplexer #(.enable("false")) multiplexer_47 (
    .in0(multiplexer_46_out), .in1(multiplexer_48_out), .out(out_82), .sel(sel_1));
  Multiplexer #(.enable("false")) multiplexer_48 (.in0(in_48), .in1(in_64), .out(multiplexer_48_out), .sel(sel_0));

  // Notes on the sheet:
  //   aMuxb[16]
  //   cMuxd[16]
endmodule
