// Logisim project mux4way_gate.circ as structural Verilog: 1 circuit, main circuit main
module main (
  input  a,
  input  b,
  input  c,
  input  d,
  input  sel_1,
  input  sel_0,
  output out
);

  wire multiplexer_1_out, multiplexer_2_out;

  Multiplexer #(.enable("false")) multiplexer_1 (.in0(a), .in1(b), .out(multiplexer_1_out), .sel(sel_0));
  Multiplexer #(.enable("false")) multiplexer_2 (.in0(c), .in1(d), .out(multiplexer_2_out), .sel(sel_0));
  Multiplexer #(.enable("false")) multiplexer_3 (
    .in0(multiplexer_1_out), .in1(multiplexer_2_out), .out(out), .sel(sel_1));
endmodule
