// Logisim project mux8way_gate.circ as structural Verilog: 1 circuit, main circuit main
module main (
  input  a,
  input  b,
  input  c,
  input  d,
  input  e,
  input  f,
  input  g,
  input  h,
  input  sel_2,
  input  sel_1,
  input  sel_0,
  output out_12
);

  wire multiplexer_1_out, multiplexer_2_out, multiplexer_3_out, multiplexer_4_out, multiplexer_5_out,
       multiplexer_7_out;

  Multiplexer #(.enable("false")) multiplexer_1 (.in0(a), .in1(b), .out(multiplexer_1_out), .sel(sel_0));
  Multiplexer #(.enable("false")) multiplexer_2 (.in0(c), .in1(d), .out(multiplexer_2_out), .sel(sel_0));
  Multiplexer #(.enable("false")) multiplexer_3 (.in0(e), .in1(f), .out(multiplexer_3_out), .sel(sel_0));
  Multiplexer #(.enable("false")) multiplexer_4 (.in0(g), .in1(h), .out(multiplexer_4_out), .sel(sel_0));
  Multiplexer #(.enable("false")) multiplexer_5 (
    .in0(multiplexer_1_out), .in1(multiplexer_2_out), .out(multiplexer_5_out), .sel(sel_1));
  Multiplexer #(.enable("false")) multiplexer_6 (
    .in0(multiplexer_5_out), .in1(multiplexer_7_out), .out(out_12), .sel(sel_2));
  Multiplexer #(.enable("false")) multiplexer_7 (
    .in0(multiplexer_3_out), .in1(multiplexer_4_out), .out(multiplexer_7_out), .sel(sel_1));
endmodule
