// Logisim project mux_gate.circ as structural Verilog: 1 circuit, main circuit main
module main (
  input  a,
  input  sel,
  input  b,
  output MUX
);

  wire AND_2_out, AND_3_out, AND_4_out, AND_5_out, AND_6_out, AND_7_out, AND_8_out, AND_out, not_1_out,
       not_2_out, not_3_out, not_4_out, OR_2_out, OR_out;

  not not_1 (not_1_out, b);
  not not_2 (not_2_out, a);
  and AND (AND_out, a, not_1_out);
  not not_3 (not_3_out, sel);
  and AND_2 (AND_2_out, a, b);
  not not_4 (not_4_out, sel);
  and AND_3 (AND_3_out, not_2_out, b);
  and AND_4 (AND_4_out, a, b);
  and AND_5 (AND_5_out, AND_out, not_3_out);
  and AND_6 (AND_6_out, AND_2_out, not_4_out);
  and AND_7 (AND_7_out, AND_3_out, sel);
  and AND_8 (AND_8_out, AND_4_out, sel);
  or OR (OR_out, AND_5_out, AND_6_out);
  or OR_2 (OR_2_out, OR_out, AND_7_out);
  or OR_3 (MUX, OR_2_out, AND_8_out);
endmodule
