// Logisim project not16_gate.circ as structural Verilog: 1 circuit, main circuit main
module main (
  input  in_16,
  input  in_2,
  input  in_3,
  input  in_4,
  input  in_5,
  input  in_6,
  input  in_7,
  input  in_8,
  input  in_9,
  input  in_10,
  input  in_11,
  input  in_12,
  input  in_13,
  input  in_14,
  input  in_15,
  input  in_16_2,
  output out_16,
  output out_18,
  output out_19,
  output out_20,
  output out_21,
  output out_22,
  output out_23,
  output out_24,
  output out_25,
  output out_26,
  output out_27,
  output out_28,
  output out_29,
  output out_30,
  output out_31,
  output out_32
);

  not not_1 (out_16, in_16);
  not not_2 (out_18, in_2);
  not not_3 (out_19, in_3);
  not not_4 (out_20, in_4);
  not not_5 (out_21, in_5);
  not not_6 (out_22, in_6);
  not not_7 (out_23, in_7);
  not not_8 (out_24, in_8);
  not not_9 (out_25, in_9);
  not not_10 (out_26, in_10);
  not not_11 (out_27, in_11);
  not not_12 (out_28, in_12);
  not not_13 (out_29, in_13);
  not not_14 (out_30, in_14);
  not not_15 (out_31, in_15);
  not not_16 (out_32, in_16_2);
endmodule
