// Logisim project or8way_gate.circ as structural Verilog: 1 circuit, main circuit main
module main (
  input  in_0,
  input  in_1,
  input  in_2,
  input  in_3,
  input  in_4,
  input  in_5,
  input  in_6,
  input  in_7,
  output out
);

  wire OR_2_out, OR_3_out, OR_4_out, OR_5_out, OR_6_out, OR_out;

  or OR (OR_out, in_0, in_1);
  or OR_2 (OR_2_out, OR_out, in_2);
  or OR_3 (OR_3_out, OR_2_out, in_3);
  or OR_4 (OR_4_out, OR_3_out, in_4);
  or OR_5 (OR_5_out, OR_4_out, in_5);
  or OR_6 (OR_6_out, OR_5_out, in_6);
  or OR_7 (out, OR_6_out, in_7);
endmodule
