// Logisim project or_gate.circ as structural Verilog: 1 circuit, main circuit main
module main (
  input  a,
  input  b,
  output out
);

  wire AND_out, not_1_out, not_2_out;

  not not_1 (not_1_out, a);
  not not_2 (not_2_out, b);
  not not_3 (out, AND_out);
  and AND (AND_out, not_1_out, not_2_out);
endmodule
