// Logisim project xor_gate.circ as structural Verilog: 1 circuit, main circuit main
module main (
  input  a,
  input  b,
  output XOR
);

  wire AND_2_out, AND_out, not_1_out, not_2_out;

  not not_1 (not_1_out, a);
  not not_2 (not_2_out, b);
  and AND (AND_out, not_1_out, b);
  and AND_2 (AND_2_out, a, not_2_out);
  or OR (XOR, AND_out, AND_2_out);
endmodule
