// Logisim project INC16PROTO.circ as structural Verilog: 1 circuit, main circuit main
module main (
  input  in_1,
  input  in_2,
  input  in_3,
  input  in_4,
  input  in_5,
  input  in_6,
  input  in_7,
  input  in_8,
  input  in_9,
  input  in_10,
  input  in_11,
  input  in_12,
  input  in_13,
  input  in_14,
  input  in_15,
  input  in_16,
  input  in_17,
  input  in_18,
  input  in_19,
  output out_20,
  output out_21,
  output out_22,
  output out_23,
  output out_24,
  output out_25,
  output out_26,
  output out_27,
  output out_28,
  output out_29,
  output out_30,
  output out_31,
  output out_32,
  output out_33,
  output out_34,
  output out_35,
  output out_36,
  output out_37
);

  wire AND_2_out, AND_3_out, AND_4_out, AND_5_out, AND_6_out, AND_7_out, AND_8_out, AND_9_out, AND_10_out,
       AND_11_out, AND_12_out, AND_13_out, AND_14_out, AND_15_out, AND_out, not_2_out, not_3_out, not_4_out,
       not_5_out, not_6_out, not_7_out, not_8_out, not_9_out, not_10_out, not_11_out, not_12_out, not_13_out,
       not_14_out, not_15_out, not_16_out, not_17_out;

  and AND (AND_out, in_1, in_2);
  and AND_2 (AND_2_out, AND_out, in_3);
  and AND_3 (AND_3_out, AND_2_out, in_5);
  and AND_4 (AND_4_out, AND_3_out, in_7);
  and AND_5 (AND_5_out, AND_4_out, in_8);
  and AND_6 (AND_6_out, AND_5_out, in_9);
  and AND_7 (AND_7_out, AND_6_out, in_10);
  and AND_8 (AND_8_out, AND_7_out, in_11);
  and AND_9 (AND_9_out, AND_8_out, in_12);
  and AND_10 (AND_10_out, AND_9_out, in_13);
  and AND_11 (AND_11_out, AND_10_out, in_14);
  and AND_12 (AND_12_out, AND_11_out, in_15);
  and AND_13 (AND_13_out, AND_12_out, in_16);
  and AND_14 (AND_14_out, AND_13_out, in_17);
  and AND_15 (AND_15_out, AND_14_out, in_18);
  // AND_Gate AND_16 has open pins: in1=AND_15_out, in4=in_19, out=open
  not not_1 (out_20, in_1);
  not not_2 (not_2_out, in_2);
  not not_3 (not_3_out, in_3);
  not not_4 (not_4_out, in_5);
  not not_5 (not_5_out, in_7);
  not not_6 (not_6_out, in_8);
  not not_7 (not_7_out, in_9);
  not not_8 (not_8_out, in_10);
  not not_9 (not_9_out, in_11);
  not not_10 (not_10_out, in_12);
  not not_11 (not_11_out, in_13);
  not not_12 (not_12_out, in_14);
  not not_13 (not_13_out, in_15);
  not not_14 (not_14_out, in_16);
  not not_15 (not_15_out, in_17);
  not not_16 (not_16_out, in_18);
  not not_17 (not_17_out, in_19);
  Multiplexer #(.enable("false")) multiplexer_1 (.in0(in_2), .in1(not_2_out), .out(out_21), .sel(in_1));
  Multiplexer #(.enable("false")) multiplexer_2 (.in0(in_3), .in1(not_3_out), .out(out_22), .sel(AND_out));
  Multiplexer #(.enable("false")) multiplexer_3 (.in0(in_5), .in1(not_4_out), .out(out_24), .sel(AND_2_out));
  Multiplexer #(.enable("false")) multiplexer_4 (.in0(in_7), .in1(not_5_out), .out(out_25), .sel(AND_3_out));
  Multiplexer #(.enable("false")) multiplexer_5 (.in0(in_8), .in1(not_6_out), .out(out_26), .sel(AND_4_out));
  Multiplexer #(.enable("false")) multiplexer_6 (.in0(in_9), .in1(not_7_out), .out(out_27), .sel(AND_5_out));
  Multiplexer #(.enable("false")) multiplexer_7 (.in0(in_10), .in1(not_8_out), .out(out_28), .sel(AND_6_out));
  Multiplexer #(.enable("false")) multiplexer_8 (.in0(in_11), .in1(not_9_out), .out(out_29), .sel(AND_7_out));
  Multiplexer #(.enable("false")) multiplexer_9 (.in0(in_12), .in1(not_10_out), .out(out_30), .sel(AND_8_out));
  Multiplexer #(.enable("false")) multiplexer_10 (.in0(in_13), .in1(not_11_out), .out(out_31), .sel(AND_9_out));
  Multiplexer #(.enable("false")) multiplexer_11 (.in0(in_14), .in1(not_12_out), .out(out_32), .sel(AND_10_out));
  Multiplexer #(.enable("false")) multiplexer_12 (.in0(in_15), .in1(not_13_out), .out(out_33), .sel(AND_11_out));
  Multiplexer #(.enable("false")) multiplexer_13 (.in0(in_16), .in1(not_14_out), .out(out_34), .sel(AND_12_out));
  Multiplexer #(.enable("false")) multiplexer_14 (.in0(in_17), .in1(not_15_out), .out(out_35), .sel(AND_13_out));
  Multiplexer #(.enable("false")) multiplexer_15 (.in0(in_18), .in1(not_16_out), .out(out_36), .sel(AND_14_out));
  Multiplexer #(.enable("false")) multiplexer_16 (.in0(in_19), .in1(not_17_out), .out(out_37), .sel(AND_15_out));
  and and_17 (out_23, in_4, in_6);
endmodule
