// Logisim project add16.circ as structural Verilog: 1 circuit, main circuit main
module main (
  input  in_1,
  input  in_2,
  input  in_3,
  input  in_4,
  input  in_5,
  input  in_6,
  input  in_7,
  input  in_8,
  input  in_9,
  input  in_10,
  input  in_11,
  input  in_12,
  input  in_13,
  input  in_14,
  input  in_15,
  input  in_16,
  input  in_17,
  input  in_18,
  input  in_19,
  input  in_20,
  input  in_21,
  input  in_22,
  input  in_23,
  input  in_24,
  input  in_25,
  input  in_26,
  input  in_27,
  input  in_28,
  input  in_29,
  input  in_30,
  input  in_31,
  input  in_32,
  output out_33,
  output out_34,
  output out_35,
  output out_36,
  output out_37,
  output out_38,
  output out_39,
  output out_40,
  output out_41,
  output out_42,
  output out_43,
  output out_44,
  output out_45,
  output out_46,
  output out_47,
  output out_48,
  output ignored_carry_bit
);

  wire AND_2_out, AND_3_out, AND_4_out, AND_5_out, AND_6_out, AND_7_out, AND_8_out, AND_9_out, AND_10_out,
       AND_11_out, AND_12_out, AND_13_out, AND_14_out, AND_15_out, AND_16_out, AND_out, multiplexer_2_out,
       multiplexer_4_out, multiplexer_6_out, multiplexer_8_out, multiplexer_10_out, multiplexer_12_out,
       multiplexer_14_out, multiplexer_16_out, multiplexer_18_out, multiplexer_20_out, multiplexer_22_out,
       multiplexer_24_out, multiplexer_26_out, multiplexer_28_out, not_1_out, not_2_out, not_3_out,
       not_4_out, not_5_out, not_6_out, not_7_out, not_8_out, not_9_out, not_10_out, not_11_out, not_12_out,
       not_13_out, not_14_out, not_15_out, OR_2_out, OR_3_out, OR_4_out, OR_5_out, OR_6_out, OR_7_out,
       OR_8_out, OR_9_out, OR_10_out, OR_11_out, OR_12_out, OR_13_out, OR_14_out, OR_15_out, OR_out,
       XOR_2_out, XOR_3_out, XOR_4_out, XOR_5_out, XOR_6_out, XOR_7_out, XOR_8_out, XOR_9_out, XOR_10_out,
       XOR_11_out, XOR_12_out, XOR_13_out, XOR_14_out, XOR_15_out, XOR_16_out, XOR_17_out, XOR_18_out,
       XOR_19_out, XOR_20_out, XOR_21_out, XOR_22_out, XOR_23_out, XOR_24_out, XOR_25_out, XOR_26_out,
       XOR_27_out, XOR_28_out, XOR_29_out, XOR_30_out, XOR_31_out;

  xor XOR (out_33, in_1, in_17);
  and AND (AND_out, in_1, in_17);
  xor XOR_2 (XOR_2_out, in_2, in_18);
  and AND_2 (AND_2_out, in_2, in_18);
  xor XOR_3 (XOR_3_out, in_2, in_18);
  or OR (OR_out, in_2, in_18);
  Multiplexer #(.enable("false")) multiplexer_1 (.in0(XOR_2_out), .in1(not_1_out), .out(out_34), .sel(AND_out));
  Multiplexer #(.enable("false")) multiplexer_2 (.in0(AND_2_out), .in1(OR_out), .out(multiplexer_2_out), .sel(AND_out));
  not not_1 (not_1_out, XOR_3_out);
  xor XOR_4 (XOR_4_out, in_3, in_19);
  and AND_3 (AND_3_out, in_3, in_19);
  xor XOR_5 (XOR_5_out, in_3, in_19);
  or OR_2 (OR_2_out, in_3, in_19);
  not not_2 (not_2_out, XOR_5_out);
  Multiplexer #(.enable("false")) multiplexer_3 (
    .in0(XOR_4_out), .in1(not_2_out), .out(out_35), .sel(multiplexer_2_out));
  Multiplexer #(.enable("false")) multiplexer_4 (
    .in0(AND_3_out), .in1(OR_2_out), .out(multiplexer_4_out), .sel(multiplexer_2_out));
  xor XOR_6 (XOR_6_out, in_4, in_20);
  and AND_4 (AND_4_out, in_4, in_20);
  xor XOR_7 (XOR_7_out, in_4, in_20);
  or OR_3 (OR_3_out, in_4, in_20);
  not not_3 (not_3_out, XOR_7_out);
  Multiplexer #(.enable("false")) multiplexer_5 (
    .in0(XOR_6_out), .in1(not_3_out), .out(out_36), .sel(multiplexer_4_out));
  Multiplexer #(.enable("false")) multiplexer_6 (
    .in0(AND_4_out), .in1(OR_3_out), .out(multiplexer_6_out), .sel(multiplexer_4_out));
  xor XOR_8 (XOR_8_out, in_5, in_21);
  and AND_5 (AND_5_out, in_5, in_21);
  not not_4 (not_4_out, XOR_9_out);
  xor XOR_9 (XOR_9_out, in_5, in_21);
  or OR_4 (OR_4_out, in_5, in_21);
  Multiplexer #(.enable("false")) multiplexer_7 (
    .in0(XOR_8_out), .in1(not_4_out), .out(out_37), .sel(multiplexer_6_out));
  Multiplexer #(.enable("false")) multiplexer_8 (
    .in0(AND_5_out), .in1(OR_4_out), .out(multiplexer_8_out), .sel(multiplexer_6_out));
  xor XOR_10 (XOR_10_out, in_6, in_22);
  and AND_6 (AND_6_out, in_6, in_22);
  not not_5 (not_5_out, XOR_11_out);
  xor XOR_11 (XOR_11_out, in_6, in_22);
  or OR_5 (OR_5_out, in_6, in_22);
  Multiplexer #(.enable("false")) multiplexer_9 (
    .in0(XOR_10_out), .in1(not_5_out), .out(out_38), .sel(multiplexer_8_out));
  Multiplexer #(.enable("false")) multiplexer_10 (
    .in0(AND_6_out), .in1(OR_5_out), .out(multiplexer_10_out), .sel(multiplexer_8_out));
  xor XOR_12 (XOR_12_out, in_7, in_23);
  and AND_7 (AND_7_out, in_7, in_23);
  xor XOR_13 (XOR_13_out, in_7, in_23);
  or OR_6 (OR_6_out, in_7, in_23);
  not not_6 (not_6_out, XOR_13_out);
  Multiplexer #(.enable("false")) multiplexer_11 (
    .in0(XOR_12_out), .in1(not_6_out), .out(out_39), .sel(multiplexer_10_out));
  Multiplexer #(.enable("false")) multiplexer_12 (
    .in0(AND_7_out), .in1(OR_6_out), .out(multiplexer_12_out), .sel(multiplexer_10_out));
  xor XOR_14 (XOR_14_out, in_8, in_24);
  and AND_8 (AND_8_out, in_8, in_24);
  xor XOR_15 (XOR_15_out, in_8, in_24);
  or OR_7 (OR_7_out, in_8, in_24);
  Multiplexer #(.enable("false")) multiplexer_13 (
    .in0(XOR_14_out), .in1(not_7_out), .out(out_40), .sel(multiplexer_12_out));
  Multiplexer #(.enable("false")) multiplexer_14 (
    .in0(AND_8_out), .in1(OR_7_out), .out(multiplexer_14_out), .sel(multiplexer_12_out));
  not not_7 (not_7_out, XOR_15_out);
  xor XOR_16 (XOR_16_out, in_9, in_25);
  and AND_9 (AND_9_out, in_9, in_25);
  xor XOR_17 (XOR_17_out, in_9, in_25);
  or OR_8 (OR_8_out, in_9, in_25);
  Multiplexer #(.enable("false")) multiplexer_15 (
    .in0(XOR_16_out), .in1(not_8_out), .out(out_41), .sel(multiplexer_14_out));
  Multiplexer #(.enable("false")) multiplexer_16 (
    .in0(AND_9_out), .in1(OR_8_out), .out(multiplexer_16_out), .sel(multiplexer_14_out));
  not not_8 (not_8_out, XOR_17_out);
  xor XOR_18 (XOR_18_out, in_10, in_26);
  and AND_10 (AND_10_out, in_10, in_26);
  xor XOR_19 (XOR_19_out, in_10, in_26);
  or OR_9 (OR_9_out, in_10, in_26);
  Multiplexer #(.enable("false")) multiplexer_17 (
    .in0(XOR_18_out), .in1(not_9_out), .out(out_42), .sel(multiplexer_16_out));
  Multiplexer #(.enable("false")) multiplexer_18 (
    .in0(AND_10_out), .in1(OR_9_out), .out(multiplexer_18_out), .sel(multiplexer_16_out));
  not not_9 (not_9_out, XOR_19_out);
  xor XOR_20 (XOR_20_out, in_11, in_27);
  and AND_11 (AND_11_out, in_11, in_27);
  xor XOR_21 (XOR_21_out, in_11, in_27);
  or OR_10 (OR_10_out, in_11, in_27);
  Multiplexer #(.enable("false")) multiplexer_19 (
    .in0(XOR_20_out), .in1(not_10_out), .out(out_43), .sel(multiplexer_18_out));
  Multiplexer #(.enable("false")) multiplexer_20 (
    .in0(AND_11_out), .in1(OR_10_out), .out(multiplexer_20_out), .sel(multiplexer_18_out));
  not not_10 (not_10_out, XOR_21_out);
  xor XOR_22 (XOR_22_out, in_12, in_28);
  and AND_12 (AND_12_out, in_12, in_28);
  xor XOR_23 (XOR_23_out, in_12, in_28);
  or OR_11 (OR_11_out, in_12, in_28);
  Multiplexer #(.enable("false")) multiplexer_21 (
    .in0(XOR_22_out), .in1(not_11_out), .out(out_44), .sel(multiplexer_20_out));
  Multiplexer #(.enable("false")) multiplexer_22 (
    .in0(AND_12_out), .in1(OR_11_out), .out(multiplexer_22_out), .sel(multiplexer_20_out));
  not not_11 (not_11_out, XOR_23_out);
  xor XOR_24 (XOR_24_out, in_13, in_29);
  and AND_13 (AND_13_out, in_13, in_29);
  not not_12 (not_12_out, XOR_25_out);
  xor XOR_25 (XOR_25_out, in_13, in_29);
  or OR_12 (OR_12_out, in_13, in_29);
  Multiplexer #(.enable("false")) multiplexer_23 (
    .in0(XOR_24_out), .in1(not_12_out), .out(out_45), .sel(multiplexer_22_out));
  Multiplexer #(.enable("false")) multiplexer_24 (
    .in0(AND_13_out), .in1(OR_12_out), .out(multiplexer_24_out), .sel(multiplexer_22_out));
  xor XOR_26 (XOR_26_out, in_14, in_30);
  and AND_14 (AND_14_out, in_14, in_30);
  not not_13 (not_13_out, XOR_27_out);
  xor XOR_27 (XOR_27_out, in_14, in_30);
  or OR_13 (OR_13_out, in_14, in_30);
  Multiplexer #(.enable("false")) multiplexer_25 (
    .in0(XOR_26_out), .in1(not_13_out), .out(out_46), .sel(multiplexer_24_out));
  Multiplexer #(.enable("false")) multiplexer_26 (
    .in0(AND_14_out), .in1(OR_13_out), .out(multiplexer_26_out), .sel(multiplexer_24_out));
  xor XOR_28 (XOR_28_out, in_15, in_31);
  and AND_15 (AND_15_out, in_15, in_31);
  xor XOR_29 (XOR_29_out, in_15, in_31);
  or OR_14 (OR_14_out, in_15, in_31);
  Multiplexer #(.enable("false")) multiplexer_27 (
    .in0(XOR_28_out), .in1(not_14_out), .out(out_47), .sel(multiplexer_26_out));
  Multiplexer #(.enable("false")) multiplexer_28 (
    .in0(AND_15_out), .in1(OR_14_out), .out(multiplexer_28_out), .sel(multiplexer_26_out));
  not not_14 (not_14_out, XOR_29_out);
  xor XOR_30 (XOR_30_out, in_16, in_32);
  and AND_16 (AND_16_out, in_16, in_32);
  xor XOR_31 (XOR_31_out, in_16, in_32);
  or OR_15 (OR_15_out, in_16, in_32);
  not not_15 (not_15_out, XOR_31_out);
  Multiplexer #(.enable("false")) multiplexer_29 (
    .in0(XOR_30_out), .in1(not_15_out), .out(out_48), .sel(multiplexer_28_out));
  Multiplexer #(.enable("false")) multiplexer_30 (
    .in0(AND_16_out), .in1(OR_15_out), .out(ignored_carry_bit), .sel(multiplexer_28_out));

  // Notes on the sheet:
  //   a[0]
  //   b[0]
  //   HALF ADDER
  //   sum[0]
  //   a[1]
  //   b[1]
  //   carry[0]
  //   FULL ADDER 1
  //   carry[1]
  //   sum[1]
  //   a[2]
  //   b[2]
  //   carry[1]
  //   FULL ADDER 2
  //   sum[1]
  //   carry[3]
  //   a[3]
  //   b[3]
  //   carry[2]
  //   FULL ADDER 3
  //   sum[3]
  //   carry[3]
  //   a[4]
  //   b[4]
  //   carry[3]
  //   FULL ADDER 4
  //   sum[4]
  //   carry[4]
  //   carry[4]
  //   a[5]
  //   b[5]
  //   FULL ADDER 5
  //   sum[5]
  //   carry[5]
  //   FULL ADDER
  //   FULL ADDER
  //   FULL ADDER
  //   FULL ADDER
  //   FULL ADDER
  //   FULL ADDER
  //   FULL ADDER
  //   FULL ADDER
  //   FULL ADDER
  //   FULL ADDER
endmodule
