// Logisim project alu.circ as structural Verilog: 1 circuit, main circuit main
module main (
  input  zx,
  input  nx,
  input  zy,
  input  ny,
  input  f,
  input  no,
  input  [15:0] x,
  input  [15:0] y,
  output [15:0] out_9,
  output [15:0] x_2,
  output [15:0] y_2,
  output [15:0] f_2,
  output zr,
  output ng
);

  wire OR_out;
  wire [15:0] adder_1_out, adder_2_out, adder_3_out, AND_out, multiplexer_1_out, multiplexer_2_out,
       not_1_out, not_2_out, not_3_out, not_4_out, not_5_out, not_6_out, not_7_out;

  assign not_1_out = ~x;  // NOT_Gate not_1, 16 bits wide
  assign not_2_out = ~y;  // NOT_Gate not_2, 16 bits wide
  assign not_3_out = ~adder_1_out;  // NOT_Gate not_3, 16 bits wide
  Adder #(.width(16)) adder_1 (.a(x), .b(not_1_out), .out(adder_1_out));  // open: cin, cout
  assign not_4_out = ~adder_2_out;  // NOT_Gate not_4, 16 bits wide
  Adder #(.width(16)) adder_2 (.a(y), .b(not_2_out), .out(adder_2_out));  // open: cin, cout
  Multiplexer #(.width(16), .enable("false")) multiplexer_1 (
    .in0(x), .in1(not_3_out), .out(multiplexer_1_out), .sel(zx));
  assign not_5_out = ~multiplexer_1_out;  // NOT_Gate not_5, 16 bits wide
  Multiplexer #(.width(16), .enable("false")) multiplexer_2 (
    .in0(y), .in1(not_4_out), .out(multiplexer_2_out), .sel(zy));
  assign not_6_out = ~multiplexer_2_out;  // NOT_Gate not_6, 16 bits wide
  Multiplexer #(.width(16), .enable("false")) multiplexer_3 (
    .in0(multiplexer_1_out), .in1(not_5_out), .out(x_2), .sel(nx));
  Multiplexer #(.width(16), .enable("false")) multiplexer_4 (
    .in0(multiplexer_2_out), .in1(not_6_out), .out(y_2), .sel(ny));
  assign AND_out = x_2 & y_2;  // AND_Gate AND, 16 bits wide
  Multiplexer #(.width(16), .enable("false")) multiplexer_5 (.in0(AND_out), .in1(adder_3_out), .out(f_2), .sel(f));
  Adder #(.width(16)) adder_3 (.a(x_2), .b(y_2), .out(adder_3_out));  // open: cin, cout
  assign not_7_out = ~f_2;  // NOT_Gate not_7, 16 bits wide
  Multiplexer #(.width(16), .enable("false")) multiplexer_6 (
    .in0(f_2), .in1(not_7_out), .out({ng, out_9[14:0]}), .sel(no));
  or OR (OR_out, ng, out_9[14], out_9[13], out_9[12], out_9[11], out_9[10], out_9[9], out_9[8], out_9[7], out_9[6], out_9[5], out_9[4], out_9[3], out_9[2], out_9[1], out_9[0]);
  not not_8 (zr, OR_out);

  assign out_9[15] = ng;
endmodule
