// Logisim project full_adder.circ as structural Verilog: 1 circuit, main circuit main
module main (
  input  a,
  input  b,
  input  c,
  output sum,
  output carry
);

  wire AND_out, not_1_out, OR_out, XOR_2_out, XOR_out;

  xor XOR (XOR_out, b, c);
  and AND (AND_out, b, c);
  xor XOR_2 (XOR_2_out, b, c);
  or OR (OR_out, b, c);
  not not_1 (not_1_out, XOR_2_out);
  Multiplexer #(.enable("false")) multiplexer_1 (.in0(XOR_out), .in1(not_1_out), .out(sum), .sel(a));
  Multiplexer #(.enable("false")) multiplexer_2 (.in0(AND_out), .in1(OR_out), .out(carry), .sel(a));

  // Notes on the sheet:
  //   Group 1
  //   Group 2
endmodule
