// Logisim project full_adder_prototypes.circ as structural Verilog: 1 circuit, main circuit main
module main (
  input  b,
  input  c,
  input  a,
  input  b_2,
  input  b_3,
  input  c_2,
  input  c_3,
  input  b_4,
  input  c_4,
  input  a_2,
  output sum,
  output carry,
  output sum_2,
  output sum_3,
  output carry_2,
  output carry_3,
  output sum_4,
  output carry_4
);

  wire AND_2_out, AND_3_out, AND_out, not_3_out, OR_3_out, xor_1_out, xor_2_out, XOR_3_out, XOR_4_out,
       XOR_5_out, XOR_6_out;

  or or_1 (carry, b, c);
  not not_1 (sum, xor_1_out);
  xor xor_1 (xor_1_out, b, c);
  and AND (AND_out, b_4, c_4);
  and AND_2 (AND_2_out, b_4, c_4);
  xor xor_2 (xor_2_out, b_2, c_2);
  or or_2 (carry_2, b_2, c_2);
  xor XOR_3 (XOR_3_out, c_4, b_4);
  xor XOR_4 (XOR_4_out, c_4, b_4);
  not not_2 (sum_2, xor_2_out);
  Multiplexer #(.enable("false")) multiplexer_1 (.in0(XOR_3_out), .in1(XOR_4_out), .out(sum_4), .sel(a_2));
  Multiplexer #(.enable("false")) multiplexer_2 (.in0(AND_out), .in1(AND_2_out), .out(carry_4), .sel(a_2));
  xor XOR_5 (XOR_5_out, b_3, c_3);
  and AND_3 (AND_3_out, b_3, c_3);
  xor XOR_6 (XOR_6_out, b_3, c_3);
  or OR_3 (OR_3_out, b_3, c_3);
  not not_3 (not_3_out, XOR_6_out);
  Multiplexer #(.enable("false")) multiplexer_3 (.in0(XOR_5_out), .in1(not_3_out), .out(sum_3), .sel(a));
  Multiplexer #(.enable("false")) multiplexer_4 (.in0(AND_3_out), .in1(OR_3_out), .out(carry_3), .sel(a));

  // Notes on the sheet:
  //   Group 1
  //   Group 2
endmodule
