// Logisim project half_adder.circ as structural Verilog: 1 circuit, main circuit main
module main (
  input  a,
  input  b,
  output sum,
  output carry
);

  and AND (carry, a, b);
  xor XOR (sum, b, a);
endmodule
