// Logisim project 16bit8registerRAM.circ as structural Verilog: 1 circuit, main circuit main
module main (
  input  load,
  input  [15:0] \input ,
  input  [2:0] address,
  input  enable,
  output [15:0] out_5,
  output [15:0] out_6,
  output [15:0] out_7,
  output [15:0] out_8,
  output [15:0] out_9,
  output [15:0] out_10,
  output [15:0] out_11,
  output [15:0] out_12
);

  wire clock_out, demultiplexer_2_out0, demultiplexer_2_out1, demultiplexer_2_out2, demultiplexer_2_out3,
       demultiplexer_2_out4, demultiplexer_2_out5, demultiplexer_2_out6, demultiplexer_2_out7;
  wire [15:0] demultiplexer_1_out0, demultiplexer_1_out1, demultiplexer_1_out2, demultiplexer_1_out3,
       demultiplexer_1_out4, demultiplexer_1_out5, demultiplexer_1_out6, demultiplexer_1_out7,
       multiplexer_1_out, multiplexer_2_out, multiplexer_3_out, multiplexer_4_out, multiplexer_5_out,
       multiplexer_6_out, multiplexer_7_out, multiplexer_8_out;

  Demultiplexer #(.select(3), .width(16), .enable("false")) demultiplexer_1 (
    .out0(demultiplexer_1_out0), .out1(demultiplexer_1_out1), .out2(demultiplexer_1_out2),
    .out3(demultiplexer_1_out3), .out4(demultiplexer_1_out4), .out5(demultiplexer_1_out5),
    .out6(demultiplexer_1_out6), .out7(demultiplexer_1_out7), .in(\input ), .sel(address));
  Demultiplexer #(.select(3), .enable("false")) demultiplexer_2 (
    .out0(demultiplexer_2_out0), .out1(demultiplexer_2_out1), .out2(demultiplexer_2_out2),
    .out3(demultiplexer_2_out3), .out4(demultiplexer_2_out4), .out5(demultiplexer_2_out5),
    .out6(demultiplexer_2_out6), .out7(demultiplexer_2_out7), .in(load), .sel(address));
  Clock clock (.out(clock_out));
  Multiplexer #(.width(16), .enable("false")) multiplexer_1 (
    .in0(out_5), .in1(demultiplexer_1_out0), .out(multiplexer_1_out), .sel(demultiplexer_2_out0));
  Register #(.width(16)) registers (.D(multiplexer_1_out), .en(enable), .Q(out_5), .clk(clock_out));  // open: clr
  Register #(.width(16)) register_1 (.D(multiplexer_2_out), .en(enable), .Q(out_6), .clk(clock_out));  // open: clr
  Multiplexer #(.width(16), .enable("false")) multiplexer_2 (
    .in0(out_6), .in1(demultiplexer_1_out1), .out(multiplexer_2_out), .sel(demultiplexer_2_out1));
  Multiplexer #(.width(16), .enable("false")) multiplexer_3 (
    .in0(out_7), .in1(demultiplexer_1_out2), .out(multiplexer_3_out), .sel(demultiplexer_2_out2));
  Register #(.width(16)) register_2 (.D(multiplexer_3_out), .en(enable), .Q(out_7), .clk(clock_out));  // open: clr
  Register #(.width(16)) register_3 (.D(multiplexer_4_out), .en(enable), .Q(out_8), .clk(clock_out));  // open: clr
  Multiplexer #(.width(16), .enable("false")) multiplexer_4 (
    .in0(out_8), .in1(demultiplexer_1_out3), .out(multiplexer_4_out), .sel(demultiplexer_2_out3));
  Register #(.width(16)) register_4 (.D(multiplexer_5_out), .en(enable), .Q(out_9), .clk(clock_out));  // open: clr
  Multiplexer #(.width(16), .enable("false")) multiplexer_5 (
    .in0(out_9), .in1(demultiplexer_1_out4), .out(multiplexer_5_out), .sel(demultiplexer_2_out4));
  Multiplexer #(.width(16), .enable("false")) multiplexer_6 (
    .in0(out_10), .in1(demultiplexer_1_out5), .out(multiplexer_6_out), .sel(demultiplexer_2_out5));
  Register #(.width(16)) register_5 (.D(multiplexer_6_out), .en(enable), .Q(out_10), .clk(clock_out));  // open: clr
  Multiplexer #(.width(16), .enable("false")) multiplexer_7 (
    .in0(out_11), .in1(demultiplexer_1_out6), .out(multiplexer_7_out), .sel(demultiplexer_2_out6));
  Register #(.width(16)) register_6 (.D(multiplexer_7_out), .en(enable), .Q(out_11), .clk(clock_out));  // open: clr
  Multiplexer #(.width(16), .enable("false")) multiplexer_8 (
    .in0(out_12), .in1(demultiplexer_1_out7), .out(multiplexer_8_out), .sel(demultiplexer_2_out7));
  Register #(.width(16)) register_7 (.D(multiplexer_8_out), .en(enable), .Q(out_12), .clk(clock_out));  // open: clr
endmodule
