// Logisim project 1bitregister_test_bench.circ as structural Verilog: 1 circuit, main circuit main
module main (
  input  in_1,
  input  in_2,
  input  [15:0] in_3,
  input  in_4,
  input  in_5,
  input  in_6,
  input  load,
  input  in_8,
  input  in,
  input  in_10,
  input  load_2,
  input  in_12,
  input  in_7,
  input  in_14,
  input  in_15,
  input  in_16,
  input  in_17,
  input  in_18,
  output out_19,
  output [15:0] out_20,
  output out_21,
  output out_22,
  output out_23,
  output out_24,
  output out_25,
  output out_26
);

  wire clock_1_out, clock_2_out, d_ff_1_q, d_ff_1_qn, multiplexer_2_out, multiplexer_3_out;

  Multiplexer #(.enable("false")) multiplexer_1 (.in0(in_1), .in1(in_2), .out(out_19), .sel(in_6));
  Clock clock_1 (.out(clock_1_out));
  Multiplexer #(.enable("false")) multiplexer_2 (.in0(out_24), .in1(in_7), .out(multiplexer_2_out), .sel(load_2));
  D_Flip_Flop #(.trigger("low")) d_ff_1 (
    .D(multiplexer_3_out), .Q(d_ff_1_q), .Qn(d_ff_1_qn), .preset(load));  // open: clk, en, reset
  Multiplexer #(.enable("false")) multiplexer_3 (.in0(in), .out(multiplexer_3_out), .sel(load));  // open: in1
  D_Flip_Flop #(.trigger("low")) d_ff_2 (
    .clk(clock_1_out), .D(multiplexer_2_out), .Q(out_24), .Qn(out_25), .preset(in_14), .en(in_15),
    .reset(in_16));
  Register #(.width(16), .trigger("high")) register_1 (
    .D(in_3), .en(in_5), .Q(out_20), .clk(clock_2_out));  // open: clr
  Clock clock_2 (.out(clock_2_out));
  nor nor_1 (out_21, in_4, out_22);
  nor nor_2 (out_22, out_21, in_8);
  nor nor_3 (out_23, in_10, in_12);
  nand nand_1 (out_26, in_17, in_18);
endmodule
