// Logisim project PC.circ as structural Verilog: 1 circuit, main circuit main
module main (
  input  inc,
  input  load,
  input  reset,
  input  [15:0] in,
  input  [15:0] inc16
);

  wire clock_1_out;
  wire [15:0] adder_1_out, adder_2_out, multiplexer_1_out, multiplexer_2_out, multiplexer_3_out, not_1_out,
       not_2_out, register_1_q;

  Multiplexer #(.width(16), .enable("false")) multiplexer_1 (
    .in0(in), .in1(adder_1_out), .out(multiplexer_1_out), .sel(inc));
  Adder #(.width(16)) adder_1 (.a(register_1_q), .b(inc16), .out(adder_1_out));  // open: cin, cout
  Multiplexer #(.width(16), .enable("false")) multiplexer_2 (
    .in0(multiplexer_1_out), .in1(in), .out(multiplexer_2_out), .sel(load));
  Adder #(.width(16)) adder_2 (.a(multiplexer_2_out), .b(not_1_out), .out(adder_2_out));  // open: cin, cout
  assign not_1_out = ~multiplexer_2_out;  // NOT_Gate not_1, 16 bits wide
  Multiplexer #(.width(16), .enable("false")) multiplexer_3 (
    .in0(multiplexer_2_out), .in1(not_2_out), .out(multiplexer_3_out), .sel(reset));
  assign not_2_out = ~adder_2_out;  // NOT_Gate not_2, 16 bits wide
  Register #(.width(16)) register_1 (.D(multiplexer_3_out), .Q(register_1_q), .clk(clock_1_out));  // open: en, clr
  Clock clock_1 (.out(clock_1_out));
endmodule
