// Logisim project RAM16K.circ as structural Verilog: 1 circuit, main circuit main
module main (
  input  [15:0] in,
  input  [10:0] address_0__11,
  input  [1:0] address_12__13,
  input  load
);

  wire clock_1_out, demultiplexer_1_out0, demultiplexer_1_out1, demultiplexer_1_out2, demultiplexer_1_out3;

  Demultiplexer #(.select(2), .enable("false")) demultiplexer_1 (
    .out0(demultiplexer_1_out0), .out1(demultiplexer_1_out1), .out2(demultiplexer_1_out2),
    .out3(demultiplexer_1_out3), .in(load), .sel(address_12__13));
  RAM #(.addrWidth(11), .dataWidth(16), .bus("separate")) ram_1 (
    .addr(address_0__11), .din(in), .str(demultiplexer_1_out0), .clk(clock_1_out));  // open: data, sel, ld, clr
  RAM #(.addrWidth(11), .dataWidth(16), .bus("separate")) ram_2 (
    .addr(address_0__11), .din(in), .str(demultiplexer_1_out1), .clk(clock_1_out));  // open: data, sel, ld, clr
  RAM #(.addrWidth(11), .dataWidth(16), .bus("separate")) ram_3 (
    .addr(address_0__11), .din(in), .str(demultiplexer_1_out2), .clk(clock_1_out));  // open: data, sel, ld, clr
  RAM #(.addrWidth(11), .dataWidth(16), .bus("separate")) ram_4 (
    .addr(address_0__11), .din(in), .str(demultiplexer_1_out3), .clk(clock_1_out));  // open: data, sel, ld, clr
  Clock clock_1 (.out(clock_1_out));
endmodule
