// Logisim project RAM64_clean.circ as structural Verilog: 1 circuit, main circuit main
module main (
  input  [15:0] in,
  input  [2:0] address_0__2,
  input  [2:0] address_3__5,
  input  load
);

  wire clock_1_out, demultiplexer_1_out0, demultiplexer_1_out1, demultiplexer_1_out2, demultiplexer_1_out3,
       demultiplexer_1_out4, demultiplexer_1_out5, demultiplexer_1_out6, demultiplexer_1_out7;

  Demultiplexer #(.select(3), .enable("false")) demultiplexer_1 (
    .out0(demultiplexer_1_out0), .out1(demultiplexer_1_out1), .out2(demultiplexer_1_out2),
    .out3(demultiplexer_1_out3), .out4(demultiplexer_1_out4), .out5(demultiplexer_1_out5),
    .out6(demultiplexer_1_out6), .out7(demultiplexer_1_out7), .in(load), .sel(address_3__5));
  RAM #(.addrWidth(3), .dataWidth(16), .bus("separate")) ram_1 (
    .addr(address_0__2), .din(in), .str(demultiplexer_1_out0), .clk(clock_1_out));  // open: data, sel, ld, clr
  RAM #(.addrWidth(3), .dataWidth(16), .bus("separate")) ram_2 (
    .addr(address_0__2), .din(in), .str(demultiplexer_1_out1), .clk(clock_1_out));  // open: data, sel, ld, clr
  RAM #(.addrWidth(3), .dataWidth(16), .bus("separate")) ram_3 (
    .addr(address_0__2), .din(in), .str(demultiplexer_1_out2), .clk(clock_1_out));  // open: data, sel, ld, clr
  RAM #(.addrWidth(3), .dataWidth(16), .bus("separate")) ram_4 (
    .addr(address_0__2), .din(in), .str(demultiplexer_1_out3), .clk(clock_1_out));  // open: data, sel, ld, clr
  Clock clock_1 (.out(clock_1_out));
  RAM #(.addrWidth(3), .dataWidth(16), .bus("separate")) ram_5 (
    .addr(address_0__2), .din(in), .str(demultiplexer_1_out4), .clk(clock_1_out));  // open: data, sel, ld, clr
  RAM #(.addrWidth(3), .dataWidth(16), .bus("separate")) ram_6 (
    .addr(address_0__2), .din(in), .str(demultiplexer_1_out5), .clk(clock_1_out));  // open: data, sel, ld, clr
  RAM #(.addrWidth(3), .dataWidth(16), .bus("separate")) ram_7 (
    .addr(address_0__2), .din(in), .str(demultiplexer_1_out6), .clk(clock_1_out));  // open: data, sel, ld, clr
  RAM #(.addrWidth(3), .dataWidth(16), .bus("separate")) ram_8 (
    .addr(address_0__2), .din(in), .str(demultiplexer_1_out7), .clk(clock_1_out));  // open: data, sel, ld, clr
endmodule
