// Logisim project bit.circ as structural Verilog: 1 circuit, main circuit main
module main (
  input  load,
  input  in,
  input  in_3,
  input  enable_time,
  input  in_5,
  output out,
  output out_7
);

  wire multiplexer_1_out, timer_out;

  Clock timer (.out(timer_out));
  D_Flip_Flop #(.trigger("low")) d_ff_1 (
    .clk(timer_out), .D(multiplexer_1_out), .Q(out), .Qn(out_7), .preset(in_3), .en(enable_time), .reset(in_5));
  Multiplexer #(.enable("false")) multiplexer_1 (.in0(out), .in1(in), .out(multiplexer_1_out), .sel(load));
endmodule
